// Logisim project MIPSxy.circ as structural Verilog: 6 circuits, main circuit main
module main (
  input  reset
);

  wire ALU_EQ, ALU_LESS, ALU_MULT, clock_1_out, ctrl_1_alu_add2_s, DM_RE, DM_WE, PC_S, RF_R1E, RF_R2E,
       RF_WA_S, RF_WD_S, RF_WE;
  wire [4:0] multiplexer_1_out;
  wire [5:0] rom_1_data_2;
  wire [9:0] pc_1_pc11_2;
  wire [25:0] rom_1_data;
  wire [31:0] alu_1_s, bit_extender_1_out, multiplexer_2_out, multiplexer_3_out, ram_1_data, rf_1_r1d,
       rf_1_r2d;

  PC pc_1 (.ir25_0(rom_1_data), .pc_s(PC_S), .reset(reset), .pc11_2(pc_1_pc11_2));
  CTRL ctrl_1 (
    .ir31_26(rom_1_data_2), .ir5_0(rom_1_data[5:0]), .alu_eq(ALU_EQ), .rf_wa_s(RF_WA_S), .rf_wd_s(RF_WD_S),
    .rf_we(RF_WE), .rf_r1e(RF_R1E), .rf_r2e(RF_R2E), .alu_add2_s(ctrl_1_alu_add2_s), .dm_we(DM_WE),
    .dm_re(DM_RE), .pc_s(PC_S), .alu_sub(ALU_MULT), .alu_less(ALU_LESS));  // open: alu_eq_2, alu_mult
  ROM #(.addrWidth(10), .dataWidth(32)) rom_1 (.addr(pc_1_pc11_2), .data({rom_1_data_2, rom_1_data}));  // open: sel
  Multiplexer #(.width(5)) multiplexer_1 (
    .in0(rom_1_data[15:11]), .in1(rom_1_data[20:16]), .out(multiplexer_1_out), .sel(RF_WA_S));  // open: en
  // Probe on rom_1_data[15:0]
  // Probe on {rom_1_data_2, rom_1_data}
  Multiplexer #(.width(32)) multiplexer_2 (
    .in0(ram_1_data), .in1(alu_1_s), .out(multiplexer_2_out), .sel(RF_WD_S));  // open: en
  RF rf_1 (
    .r1a(rom_1_data[25:21]), .r2a(rom_1_data[20:16]), .we(RF_WE), .wa(multiplexer_1_out), .r1d(rf_1_r1d),
    .r2d(rf_1_r2d), .r1e(RF_R1E), .r2e(RF_R2E), .wd(multiplexer_2_out));
  // Probe on rom_1_data_2
  // Probe on rom_1_data[25:21]
  // Probe on rom_1_data[20:16]
  // Probe on rf_1_r1d
  // Probe on rf_1_r2d
  // Probe on rf_1_r1d[11:2]
  assign bit_extender_1_out = {{16{rom_1_data[15]}}, rom_1_data[15:0]};  // Bit_Extender bit_extender_1
  Multiplexer #(.width(32)) multiplexer_3 (
    .in0(bit_extender_1_out), .in1(rf_1_r2d), .out(multiplexer_3_out), .sel(ctrl_1_alu_add2_s));  // open: en
  ALU alu_1 (
    .less(ALU_MULT), .mul(ALU_MULT), .sub(ALU_MULT), .a(rf_1_r1d), .b(multiplexer_3_out), .s(alu_1_s),
    .eq(ALU_EQ));  // open: less_2
  // Probe on multiplexer_3_out
  RAM #(.addrWidth(10), .dataWidth(32), .bus("separate")) ram_1 (
    .addr(rf_1_r1d[11:2]), .din(rf_1_r2d), .data(ram_1_data), .str(DM_WE), .clk(clock_1_out), .ld(DM_RE));  // open: sel, clr
  Clock clock_1 (.out(clock_1_out));
  // Probe on alu_1_s
  // also tied to GND on the sheet: ALU_MULT

  // Other names for the same wires on the sheet: ALU_SUB = ALU_MULT

  // Notes on the sheet:
  //   contents of rom_1 (hex, n*v repeats v):
  //   20080000 20090001 200a0002 200b0003 200c0004 200d0005 200e0006 200f0007 ad080000 ad290004 ad4a0008
  //   ad6b000c ad8c0010 adad0014 adce0018 adef001c 1084020 1294820 14a5020 16b5820 18c6020 1ad6820 1ce7020
  //   1ef7820 2108fff9 2129fffa 214afffb 216bfffc 218cfffd 21adfffe 21ceffff 21ef0000 8d080000 8d290004
  //   8d4a0008 8d6b000c 8d8c0010 8dad0014 8dce0018 8def001c 4020 4820 5020 5820 6020 6820 7020 7820
  //   20087fff ad280000 ad280004 ad280008 ad28000c ad280010 ad280014 ad280018 ad28001c ad280000 20088000
  //   ad280000 21290004 ad280000 21290008 ad280000 2129000c ad280000 21290010 ad280000 21290014
endmodule

module ALU (
  input  less,
  input  mul,
  input  sub,
  input  [31:0] a,
  input  [31:0] b,
  output [31:0] s,
  output eq,
  output less_2
);

  wire buffer_1_out;
  wire [1:0] priority_encoder_1_out;
  wire [31:0] adder_1_out, bit_extender_1_out, multiplexer_1_out, multiplier_1_out, not_1_out;

  Multiplexer #(.width(32)) multiplexer_1 (.in0(b), .in1(not_1_out), .out(multiplexer_1_out), .sel(sub));  // open: en
  assign not_1_out = ~b;  // NOT_Gate not_1, 32 bits wide
  buf buffer_1 (buffer_1_out, sub);
  Adder #(.width(32)) adder_1 (.a(a), .b(multiplexer_1_out), .out(adder_1_out), .cin(sub));  // open: cout
  Multiplier #(.width(32)) multiplier_1 (.a(a), .b(b), .out(multiplier_1_out));  // open: cin, cout
  Comparator #(.width(32)) comparator_1 (.a(a), .b(b), .eq(eq), .lt(less_2));  // open: gt
  Priority_Encoder #(.select(2), .disabled(0)) priority_encoder_1 (
    .in0(1'b1), .in1(buffer_1_out), .in2(mul), .in3(less), .out(priority_encoder_1_out));  // open: gs, en_out, en_in
  assign bit_extender_1_out = {{31{1'b0}}, less_2};  // Bit_Extender bit_extender_1
  // Probe on priority_encoder_1_out
  Multiplexer #(.select(2), .width(32)) multiplexer_2 (
    .in0(adder_1_out), .in1(adder_1_out), .in2(multiplier_1_out), .in3(bit_extender_1_out), .out(s),
    .sel(priority_encoder_1_out));  // open: en
endmodule

module RF (
  input  r1e,
  input  [4:0] r1a,
  input  r2e,
  input  [4:0] r2a,
  input  [31:0] wd,
  input  we,
  input  [4:0] wa,
  output [31:0] r1d,
  output [31:0] r2d
);

  wire clock_1_out, E0, E1, E2, E3, E4, E5, E6, E7;
  wire [31:0] T0, T1, T2, T3, T4, T5, T6, T7;

  Register #(.width(32)) u_t0 (.D(wd), .en(E0), .Q(T0), .clk(clock_1_out));  // open: clr
  Register #(.width(32)) u_t1 (.D(wd), .en(E1), .Q(T1), .clk(clock_1_out));  // open: clr
  Register #(.width(32)) u_t2 (.D(wd), .en(E2), .Q(T2), .clk(clock_1_out));  // open: clr
  Register #(.width(32)) u_t3 (.D(wd), .en(E3), .Q(T3), .clk(clock_1_out));  // open: clr
  Clock clock_1 (.out(clock_1_out));
  Register #(.width(32)) u_t4 (.D(wd), .en(E4), .Q(T4), .clk(clock_1_out));  // open: clr
  Register #(.width(32)) u_t5 (.D(wd), .en(E5), .Q(T5), .clk(clock_1_out));  // open: clr
  Register #(.width(32)) u_t6 (.D(wd), .en(E6), .Q(T6), .clk(clock_1_out));  // open: clr
  Register #(.width(32)) u_t7 (.D(wd), .en(E7), .Q(T7), .clk(clock_1_out));  // open: clr
  Decoder #(.select(3), .disabled(0)) decoder_1 (
    .out0(E0), .out1(E1), .out2(E2), .out3(E3), .out4(E4), .out5(E5), .out6(E6), .out7(E7), .sel(wa[2:0]),
    .en(we));
  Multiplexer #(.select(3), .width(32)) multiplexer_1 (
    .in0(T0), .in1(T1), .in2(T2), .in3(T3), .in4(T4), .in5(T5), .in6(T6), .in7(T7), .out(r1d),
    .sel(r1a[2:0]), .en(r1e));
  Multiplexer #(.select(3), .width(32)) multiplexer_2 (
    .in0(T0), .in1(T1), .in2(T2), .in3(T3), .in4(T4), .in5(T5), .in6(T6), .in7(T7), .out(r2d),
    .sel(r2a[2:0]), .en(r2e));
endmodule

module PC (
  input  pc_s,
  input  reset,
  input  [25:0] ir25_0,
  output [9:0] pc11_2
);

  wire clock_1_out;
  wire [31:0] adder_1_out, multiplexer_1_out, pc_q;

  Adder #(.width(32)) adder_1 (.a({pc_q[31:12], pc11_2, pc_q[1:0]}), .b(32'h4), .out(adder_1_out));  // open: cin, cout
  Multiplexer #(.width(32)) multiplexer_1 (
    .in0(adder_1_out), .in1({adder_1_out[31:28], ir25_0, 2'b00}), .out(multiplexer_1_out), .sel(pc_s));  // open: en
  // Probe on {pc_q[31:12], pc11_2, pc_q[1:0]}
  Register #(.width(32)) pc (
    .D(multiplexer_1_out), .Q({pc_q[31:12], pc11_2, pc_q[1:0]}), .clk(clock_1_out), .clr(reset));  // open: en
  Clock clock_1 (.out(clock_1_out));
endmodule

module CTRL (
  input  [5:0] ir31_26,
  input  [5:0] ir5_0,
  input  alu_eq,
  output rf_wa_s,
  output rf_wd_s,
  output rf_we,
  output rf_r1e,
  output rf_r2e,
  output alu_add2_s,
  output dm_we,
  output dm_re,
  output pc_s,
  output alu_sub,
  output alu_less,
  output alu_eq_2,
  output alu_mult
);

  wire and_1_out, and_3_out, and_4_out, and_5_out, and_6_out, and_7_out, and_8_out, and_9_out,
       comparator_3_eq, comparator_4_eq, comparator_5_eq, comparator_6_eq, comparator_7_eq, comparator_8_eq,
       comparator_9_eq, comparator_10_eq, comparator_11_eq, comparator_12_eq, comparator_13_eq,
       comparator_14_eq, comparator_16_eq, comparator_17_eq, comparator_18_eq, comparator_20_eq,
       comparator_22_eq, comparator_23_eq, not_1_out;

  Comparator #(.width(6)) comparator_1 (.a(ir31_26), .b(6'b100011), .eq(dm_re));  // open: gt, lt
  Comparator #(.width(6)) comparator_2 (.a(ir31_26), .b(6'b101011), .eq(dm_we));  // open: gt, lt
  Comparator #(.width(6)) comparator_3 (.a(ir31_26), .b(6'b001000), .eq(comparator_3_eq));  // open: gt, lt
  Comparator #(.width(6)) comparator_4 (.a(ir31_26), .b({6{1'b0}}), .eq(comparator_4_eq));  // open: gt, lt
  Comparator #(.width(6)) comparator_5 (.a(ir5_0), .b(6'b100000), .eq(comparator_5_eq));  // open: gt, lt
  Comparator #(.width(6)) comparator_6 (.a(ir31_26), .b({6{1'b0}}), .eq(comparator_6_eq));  // open: gt, lt
  Comparator #(.width(6)) comparator_7 (.a(ir5_0), .b(6'b100010), .eq(comparator_7_eq));  // open: gt, lt
  Comparator #(.width(6)) comparator_8 (.a(ir31_26), .b(6'b000100), .eq(comparator_8_eq));  // open: gt, lt
  Comparator #(.width(6)) comparator_9 (.a(ir5_0), .b(6'b011000), .eq(comparator_9_eq));  // open: gt, lt
  Comparator #(.width(6)) comparator_10 (.a(ir31_26), .b({6{1'b0}}), .eq(comparator_10_eq));  // open: gt, lt
  Comparator #(.width(6)) comparator_11 (.a(ir5_0), .b(6'b010010), .eq(comparator_11_eq));  // open: gt, lt
  Comparator #(.width(6)) comparator_12 (.a(ir31_26), .b(6'b000100), .eq(comparator_12_eq));  // open: gt, lt
  not not_1 (not_1_out, comparator_13_eq);
  Comparator #(.width(6)) comparator_13 (.a(ir5_0), .b(6'b011000), .eq(comparator_13_eq));  // open: gt, lt
  Comparator #(.width(6)) comparator_14 (.a(ir31_26), .b(6'b000101), .eq(comparator_14_eq));  // open: gt, lt
  Comparator #(.width(6)) comparator_15 ();  // open: a, b, gt, eq, lt
  Comparator #(.width(6)) comparator_16 (.a(ir31_26), .b({6{1'b0}}), .eq(comparator_16_eq));  // open: gt, lt
  Comparator #(.width(6)) comparator_17 (.a(ir5_0), .b(6'b100110), .eq(comparator_17_eq));  // open: gt, lt
  Comparator #(.width(6)) comparator_18 (.a(ir31_26), .b(6'b000010), .eq(comparator_18_eq));  // open: gt, lt
  Comparator #(.width(6)) comparator_19 ();  // open: a, b, gt, eq, lt
  Comparator #(.width(6)) comparator_20 (.a(ir31_26), .b(6'b000011), .eq(comparator_20_eq));  // open: gt, lt
  Comparator #(.width(6)) comparator_21 ();  // open: a, b, gt, eq, lt
  Comparator #(.width(6)) comparator_22 (.a(ir31_26), .b({6{1'b0}}), .eq(comparator_22_eq));  // open: gt, lt
  Comparator #(.width(6)) comparator_23 (.a(ir5_0), .b(6'b001000), .eq(comparator_23_eq));  // open: gt, lt
  and and_1 (and_1_out, comparator_4_eq, comparator_5_eq);
  and and_2 (alu_sub, comparator_6_eq, comparator_7_eq);
  and and_3 (and_3_out, comparator_8_eq, comparator_9_eq);
  and and_4 (and_4_out, comparator_10_eq, comparator_11_eq);
  and and_5 (and_5_out, comparator_12_eq, not_1_out);
  and and_6 (and_6_out, comparator_16_eq, comparator_17_eq);
  and and_7 (and_7_out, comparator_22_eq, comparator_23_eq);
  and and_8 (and_8_out, and_5_out, alu_eq);
  and and_9 (and_9_out, ~alu_eq, comparator_14_eq);  // AND_Gate
  or or_1 (rf_wa_s, dm_re, comparator_3_eq);
  or or_2 (rf_wd_s, and_1_out, comparator_3_eq, and_6_out, alu_sub);
  or or_3 (rf_we, dm_re, comparator_3_eq, alu_sub, and_1_out, and_6_out);
  or or_4 (rf_r1e, and_1_out, dm_re, dm_we, comparator_3_eq, alu_sub, and_5_out, comparator_14_eq, and_6_out);
  or or_5 (rf_r2e, dm_we, and_1_out, alu_sub, and_5_out, comparator_14_eq, and_6_out);
  or or_6 (alu_add2_s, and_1_out, alu_sub, and_5_out, comparator_14_eq, and_6_out);
  or or_7 (pc_s, and_8_out, and_9_out, comparator_18_eq, comparator_20_eq);

  // Notes on the sheet:
  //   lw
  //   sw
  //   addi
  //   add
  //   sub
  //   mult
  //   mflo
  //   beq
  //   bne
  //   slt
  //   j
  //   jal
  //   jr
endmodule

module CTRLif (
  input  [5:0] ir5_0,
  input  [5:0] ir31_26,
  output ir0,
  output ir1,
  output ir2,
  output ir3,
  output ir4,
  output ir5,
  output ir26,
  output i2r7,
  output ir28,
  output ir29,
  output ir30,
  output ir31
);


  assign i2r7 = ir31_26[1];
  assign ir0 = ir5_0[0];
  assign ir1 = ir5_0[1];
  assign ir2 = ir5_0[2];
  assign ir3 = ir5_0[3];
  assign ir4 = ir5_0[4];
  assign ir5 = ir5_0[5];
  assign ir26 = ir31_26[0];
  assign ir28 = ir31_26[2];
  assign ir29 = ir31_26[3];
  assign ir30 = ir31_26[4];
  assign ir31 = ir31_26[5];
endmodule
